# Fritzing sketch sketch (saved by Fritzing 0.9.3b)
breadboards: 1

parts:
  Raspberry_Pi_1 = Raspberry Pi 3 [part_number=RPI-3-V1.2]
  R1 = Resistor [tolerance=±5% resistance=1.5k package=THT]
  LED1 = LED - 5mm [color="Red (633nm)" package="5 mm [THT]"]
  S1 = Pushbutton [package="[THT]"]
  R2 = Resistor [tolerance=±5% resistance=1.5k package=THT]

nets:
  N1: Raspberry_Pi_1.3v3, R2.Pin_0
  N2: Raspberry_Pi_1.GIPO19, S1.Pin_3, S1.Pin_4
  N3: Raspberry_Pi_1.GIPO26, R1.Pin_1
  N4: Raspberry_Pi_1.GND, LED1.anode
  N5: R1.Pin_0, LED1.cathode
  N6: S1.Pin_1, S1.Pin_2, R2.Pin_1
